# Fritzing sketch schematics (saved by Fritzing 0.9.3b)
breadboards: 1

parts:
  S1 = H-Bridge with L298N
  Part1 = Arduino Uno (Rev3)
  BAT1 = BC9VPC [package=bc9vpc]
  Part2 = Bluetooth HC-05 Macho
  M1 = DC Motor
  M2 = DC Motor

nets:
  12V: S1.12V, Part1.VIN, BAT1.V+
  GND: S1.GND, Part1.GND, BAT1.V-, Part2.GND
  N1: S1.ENA, Part1.D9_PWM
  N2: S1.IN1, Part1.D2
  N3: S1.IN2, Part1.D3_PWM
  N4: S1.IN3, Part1.D4
  N5: S1.IN4, Part1.D5_PWM
  N6: S1.ENB, Part1.D10_PWM/SS
  N7: S1.M1-01, M1.pin_2
  N8: S1.M1-02, M1.pin_1
  N9: S1.M2-01, M2.pin_2
  N10: S1.M2-02, M2.pin_1
  N11: Part1.D0/RX, Part2.TXD
  3V3: Part1.3V3, Part2.VCC

custom parts:
  H-Bridge with L298N: h-bridge
